// Logisim project CRC16_Simulation_Logism.circ as structural Verilog: 1 circuit, main circuit main
module main (
);

  wire n7404_hex_inverters_1_p2, n7486_quad_2_input_xors_1_p3,
       n74194_4_bit_bidirectional_universal_shift_register_1_p1,
       n74194_4_bit_bidirectional_universal_shift_register_1_p3,
       n74194_4_bit_bidirectional_universal_shift_register_1_p4,
       n74194_4_bit_bidirectional_universal_shift_register_1_p5,
       n74194_4_bit_bidirectional_universal_shift_register_1_p7,
       n74194_4_bit_bidirectional_universal_shift_register_1_p9,
       n74194_4_bit_bidirectional_universal_shift_register_1_p11,
       n74194_4_bit_bidirectional_universal_shift_register_1_p12,
       n74194_4_bit_bidirectional_universal_shift_register_2_p6,
       n74194_4_bit_bidirectional_universal_shift_register_2_p7,
       n74194_4_bit_bidirectional_universal_shift_register_2_p11,
       n74194_4_bit_bidirectional_universal_shift_register_3_p2,
       n74194_4_bit_bidirectional_universal_shift_register_3_p9,
       n74194_4_bit_bidirectional_universal_shift_register_3_p11,
       n74194_4_bit_bidirectional_universal_shift_register_3_p13,
       n74194_4_bit_bidirectional_universal_shift_register_3_p14,
       n74194_4_bit_bidirectional_universal_shift_register_4_p2,
       n74194_4_bit_bidirectional_universal_shift_register_4_p9,
       n74194_4_bit_bidirectional_universal_shift_register_4_p11,
       n74194_4_bit_bidirectional_universal_shift_register_4_p13,
       n74194_4_bit_bidirectional_universal_shift_register_4_p16;

  LED _13 (.in(n74194_4_bit_bidirectional_universal_shift_register_1_p7));
  LED _14 (.in(n74194_4_bit_bidirectional_universal_shift_register_1_p5));
  LED _15 (.in(n74194_4_bit_bidirectional_universal_shift_register_1_p4));
  LED _12 (.in(n74194_4_bit_bidirectional_universal_shift_register_1_p9));
  // _74194___4_bit_Bidirectional_Universal_Shift_Register 74194_4_bit_bidirectional_universal_shift_register_1: pin names not known; wires that end beside it: n74194_4_bit_bidirectional_universal_shift_register_1_p1, 1'b1, n74194_4_bit_bidirectional_universal_shift_register_1_p3, n74194_4_bit_bidirectional_universal_shift_register_1_p4, n74194_4_bit_bidirectional_universal_shift_register_1_p5, n74194_4_bit_bidirectional_universal_shift_register_1_p5, n74194_4_bit_bidirectional_universal_shift_register_1_p7, n74194_4_bit_bidirectional_universal_shift_register_1_p7, n74194_4_bit_bidirectional_universal_shift_register_1_p9, n74194_4_bit_bidirectional_universal_shift_register_1_p9, n74194_4_bit_bidirectional_universal_shift_register_1_p11, n74194_4_bit_bidirectional_universal_shift_register_1_p12
  LED _10 (.in(n74194_4_bit_bidirectional_universal_shift_register_2_p7));
  LED _8 (.in(n74194_4_bit_bidirectional_universal_shift_register_2_p11));
  LED _9 (.in(n74194_4_bit_bidirectional_universal_shift_register_1_p1));
  LED _11 (.in(n74194_4_bit_bidirectional_universal_shift_register_2_p6));
  LED _7 (.in(n74194_4_bit_bidirectional_universal_shift_register_3_p2));
  LED _5 (.in(n74194_4_bit_bidirectional_universal_shift_register_3_p11));
  LED _6 (.in(n74194_4_bit_bidirectional_universal_shift_register_3_p9));
  // _74194___4_bit_Bidirectional_Universal_Shift_Register 74194_4_bit_bidirectional_universal_shift_register_2: pin names not known; wires that end beside it: 1'b1, 1'b1, 1'b0, 1'b1, n74194_4_bit_bidirectional_universal_shift_register_1_p3, n74194_4_bit_bidirectional_universal_shift_register_2_p6, n74194_4_bit_bidirectional_universal_shift_register_2_p7, n74194_4_bit_bidirectional_universal_shift_register_2_p7, n74194_4_bit_bidirectional_universal_shift_register_1_p1, n74194_4_bit_bidirectional_universal_shift_register_1_p1, n74194_4_bit_bidirectional_universal_shift_register_2_p11, n74194_4_bit_bidirectional_universal_shift_register_2_p11
  LED _1 (.in(n74194_4_bit_bidirectional_universal_shift_register_4_p11));
  LED _4 (.in(n74194_4_bit_bidirectional_universal_shift_register_3_p13));
  LED _2 (.in(n74194_4_bit_bidirectional_universal_shift_register_4_p9));
  LED _3 (.in(n74194_4_bit_bidirectional_universal_shift_register_4_p2));
  // _74194___4_bit_Bidirectional_Universal_Shift_Register 74194_4_bit_bidirectional_universal_shift_register_3: pin names not known; wires that end beside it: n74194_4_bit_bidirectional_universal_shift_register_1_p11, n74194_4_bit_bidirectional_universal_shift_register_3_p2, 1'b1, 1'b1, 1'b0, 1'b1, n74194_4_bit_bidirectional_universal_shift_register_1_p3, n74194_4_bit_bidirectional_universal_shift_register_3_p2, n74194_4_bit_bidirectional_universal_shift_register_3_p9, n74194_4_bit_bidirectional_universal_shift_register_3_p9, n74194_4_bit_bidirectional_universal_shift_register_3_p11, n74194_4_bit_bidirectional_universal_shift_register_3_p11, n74194_4_bit_bidirectional_universal_shift_register_3_p13, n74194_4_bit_bidirectional_universal_shift_register_3_p14
  LED _0 (.in(n74194_4_bit_bidirectional_universal_shift_register_4_p13));
  // _74194___4_bit_Bidirectional_Universal_Shift_Register 74194_4_bit_bidirectional_universal_shift_register_4: pin names not known; wires that end beside it: n74194_4_bit_bidirectional_universal_shift_register_1_p11, n74194_4_bit_bidirectional_universal_shift_register_4_p2, 1'b1, 1'b1, 1'b0, 1'b1, n74194_4_bit_bidirectional_universal_shift_register_1_p3, n74194_4_bit_bidirectional_universal_shift_register_4_p2, n74194_4_bit_bidirectional_universal_shift_register_4_p9, n74194_4_bit_bidirectional_universal_shift_register_4_p9, n74194_4_bit_bidirectional_universal_shift_register_4_p11, n74194_4_bit_bidirectional_universal_shift_register_4_p11, n74194_4_bit_bidirectional_universal_shift_register_4_p13, n74194_4_bit_bidirectional_universal_shift_register_4_p13, n74194_4_bit_bidirectional_universal_shift_register_1_p11, n74194_4_bit_bidirectional_universal_shift_register_4_p16, 1'b1, 1'b1, 1'b0
  // _7486__Quad_2_Input_XOR_Gates 7486_quad_2_input_xors_1: pin names not known; wires that end beside it: n74194_4_bit_bidirectional_universal_shift_register_4_p9, 1'b1, n7486_quad_2_input_xors_1_p3, n74194_4_bit_bidirectional_universal_shift_register_1_p4, n74194_4_bit_bidirectional_universal_shift_register_4_p16, n74194_4_bit_bidirectional_universal_shift_register_3_p13, n74194_4_bit_bidirectional_universal_shift_register_2_p6, n74194_4_bit_bidirectional_universal_shift_register_1_p4, n74194_4_bit_bidirectional_universal_shift_register_1_p4, n74194_4_bit_bidirectional_universal_shift_register_3_p14, n74194_4_bit_bidirectional_universal_shift_register_1_p12, 1'b0
  // _7404__Hex_Inverters 7404_hex_inverters_1: pin names not known; wires that end beside it: 1'b1, n7404_hex_inverters_1_p2, n74194_4_bit_bidirectional_universal_shift_register_1_p3, 1'b0
  LED R (.in(n7404_hex_inverters_1_p2));
  LED CK (.in(n74194_4_bit_bidirectional_universal_shift_register_1_p11));
  LED IN (.in(n7486_quad_2_input_xors_1_p3));
  Button button_1 (.out(n7404_hex_inverters_1_p2));
  Clock clock_1 (.out(n74194_4_bit_bidirectional_universal_shift_register_1_p11));
  Button button_2 (.out(n7486_quad_2_input_xors_1_p3));
endmodule
